# Fritzing sketch PerfBoard_Sketch (saved by Fritzing 0.9.3b)
perfboards: 1

parts:
  J1 = single row smd female pin header, 15 pins [form="♀ (female)"]
  J2 = single row smd female pin header, 15 pins [form="♀ (female)"]
  M1 = DOIT Esp32 DevKit v1 (30 pins long, 11 pins width) [part_number=ESP32S-PIN30]
  J3 = female pin header, 15 pins [form="♀ (female)"]
  J4 = female pin header, 15 pins [form="♀ (female)"]
  Pololu_A1 = Pololu A4988 [package=SO16]
  J5 = female pin header, 8 pins [form="♀ (female)"]
  J6 = female pin header, 8 pins [form="♀ (female)"]
  J7 = female pin header, 2 pins [form="♀ (female)"]
  J8 = female pin header, 2 pins [form="♀ (female)"]
  J9 = female pin header, 8 pins [form="♀ (female)"]
  J10 = female pin header, 8 pins [form="♀ (female)"]
  Pololu_A2 = Pololu A4988 [package=SO16]
  J11 = female pin header, 8 pins [form="♀ (female)"]
  J12 = female pin header, 8 pins [form="♀ (female)"]
  J13 = female pin header, 2 pins [form="♀ (female)"]
  J14 = female pin header, 2 pins [form="♀ (female)"]

nets:
  N1: J1.pin1, M1.VIN, J4.pin1
  N2: J1.pin2, J2.pin2, M1.GND, J3.pin2, J4.pin2, J10.pin1, Pololu_A2.ENABLE, Pololu_A2.MS1, Pololu_A2.MS2, Pololu_A2.MS3, Pololu_A2.GND#8, J11.pin5, J11.pin6, J11.pin7, J11.pin8
  N3: J1.pin3, M1.D13, J4.pin3
  N4: J1.pin4, M1.D12, J4.pin4
  N5: J1.pin5, M1.D14, J4.pin5
  N6: J1.pin6, M1.D27, J4.pin6
  N7: J1.pin7, M1.D26, J4.pin7
  N8: J1.pin8, M1.D25, J4.pin8
  N9: J1.pin9, M1.D33, J4.pin9
  N10: J1.pin10, M1.D32, J4.pin10
  N11: J1.pin11, M1.D35, J4.pin11
  N12: J1.pin12, M1.D34, J4.pin12
  N13: J1.pin13, M1.VN, J4.pin13
  N14: J1.pin14, M1.VP, J4.pin14
  N15: J1.pin15, M1.EN, J4.pin15
  VDD: J2.pin1, M1.3V3, J3.pin1, Pololu_A1.RESET, Pololu_A1.SLEEP, Pololu_A1.VDD, J5.pin5, J5.pin6, J6.pin7, J10.pin2, Pololu_A2.RESET, Pololu_A2.SLEEP, Pololu_A2.VDD, J11.pin3, J11.pin4
  N16: J2.pin3, M1.D15, J3.pin3
  N17: J2.pin4, M1.D2, J3.pin4
  N18: J2.pin5, M1.D4, J3.pin5
  N19: J2.pin6, M1.RX2, J3.pin6
  N20: J2.pin7, M1.TX2, J3.pin7
  N21: J2.pin8, M1.D5, J3.pin8
  N22: J2.pin9, M1.D18, J3.pin9
  N23: J2.pin10, M1.D19, J3.pin10
  N24: J2.pin11, M1.D21, J3.pin11
  N25: J2.pin12, M1.RX0, J3.pin12
  N26: J2.pin13, M1.TX0, J3.pin13
  N27: J2.pin14, M1.D22, J3.pin14
  N28: J2.pin15, M1.D23, J3.pin15
  N29: Pololu_A1.ENABLE, Pololu_A1.MS1, Pololu_A1.MS2, Pololu_A1.MS3, Pololu_A1.GND#8, J5.pin1, J5.pin2, J5.pin3, J5.pin4, J6.pin8
  N30: Pololu_A1.STEP, J5.pin7
  N31: Pololu_A1.DIR, J5.pin8
  N32: Pololu_A1.1B, J6.pin6, J9.pin7, J9.pin8
  N33: Pololu_A1.1A, J6.pin5, J9.pin5, J9.pin6
  N34: Pololu_A1.2A, J6.pin4, J9.pin3, J9.pin4
  N35: Pololu_A1.2B, J6.pin3, J9.pin1, J9.pin2
  N36: Pololu_A1.GND#14, J6.pin2, J7.pin1, J7.pin2
  N37: Pololu_A1.VMOT, J6.pin1, J8.pin1, J8.pin2
  N38: J10.pin3, Pololu_A2.1B, J12.pin1, J12.pin2
  N39: J10.pin4, Pololu_A2.1A, J12.pin3, J12.pin4
  N40: J10.pin5, Pololu_A2.2A, J12.pin5, J12.pin6
  N41: J10.pin6, Pololu_A2.2B, J12.pin7, J12.pin8
  N42: J10.pin7, Pololu_A2.GND#14, J14.pin1, J14.pin2
  N43: J10.pin8, Pololu_A2.VMOT, J13.pin1, J13.pin2
  N44: Pololu_A2.STEP, J11.pin2
  N45: Pololu_A2.DIR, J11.pin1

custom parts:
  DOIT Esp32 DevKit v1 (30 pins long, 11 pins width): The DOIT Esp32 DevKit v1 is one of the development board created by DOIT to evaluate the ESP-WROOM-32 module. It is based on the ESP32 microcontroller that boasts Wifi, Bluetooth, Ethernet and Low Power support all in a single chip. (vanepp) made breadboard work, adjusted pin numbering and labels and reduced size of schematic and cleaned up pcb. This chip is 30pins long (2 x15) and 11 pins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
